# Fritzing sketch mh-et-live-esp32-mini-mh-z19 (saved by Fritzing 0.9.3b)

parts:
  WeMos_D1_Mini_Dual_Base_Shield1 = WeMos D1 Mini Dual Base Shield
  WeMos_D1_Mini_Protoboard_Shield1 = WeMos D1 Mini Protoboard Shield
  D1 = Schottky Diode [part_number="Schottky Diode for reset" package="300 mil [THT]"]
  TD-er1 = MH-Z19 CO2 sensor [part_number=MH-Z19]
  MH-ET_Live_Minikit_for_ESP1 = MH-ET Live Minikit for ESP32
  WeMos_D1_Mini_OLED_Shield1 = WeMos D1 Mini OLED Shield

nets:
  3V3: WeMos_D1_Mini_Dual_Base_Shield1.3V3_Left, WeMos_D1_Mini_Dual_Base_Shield1.3V3_Right, WeMos_D1_Mini_Protoboard_Shield1.3V3, MH-ET_Live_Minikit_for_ESP1.3.3V, WeMos_D1_Mini_OLED_Shield1.3V3
  5V: WeMos_D1_Mini_Dual_Base_Shield1.5V_Left, WeMos_D1_Mini_Dual_Base_Shield1.5V_Right, WeMos_D1_Mini_Protoboard_Shield1.5V, WeMos_D1_Mini_Protoboard_Shield1.X7-Y8, TD-er1.Vin, MH-ET_Live_Minikit_for_ESP1.VCC, WeMos_D1_Mini_OLED_Shield1.5V
  N1: WeMos_D1_Mini_Dual_Base_Shield1.A0_Left, WeMos_D1_Mini_Dual_Base_Shield1.A0_Right, WeMos_D1_Mini_Protoboard_Shield1.A0, MH-ET_Live_Minikit_for_ESP1.SVP, WeMos_D1_Mini_OLED_Shield1.A0
  N2: WeMos_D1_Mini_Dual_Base_Shield1.D0_Left, WeMos_D1_Mini_Dual_Base_Shield1.D0_Right, WeMos_D1_Mini_Protoboard_Shield1.D0, WeMos_D1_Mini_Protoboard_Shield1.X2-Y3, WeMos_D1_Mini_Protoboard_Shield1.X3-Y5, D1.cathode, MH-ET_Live_Minikit_for_ESP1.IO26, WeMos_D1_Mini_OLED_Shield1.D0
  N3: WeMos_D1_Mini_Dual_Base_Shield1.D1_Left, WeMos_D1_Mini_Dual_Base_Shield1.D1_Right, WeMos_D1_Mini_Protoboard_Shield1.D1, MH-ET_Live_Minikit_for_ESP1.IO22, WeMos_D1_Mini_OLED_Shield1.D1
  N4: WeMos_D1_Mini_Dual_Base_Shield1.D2_Left, WeMos_D1_Mini_Dual_Base_Shield1.D2_Right, WeMos_D1_Mini_Protoboard_Shield1.D2, MH-ET_Live_Minikit_for_ESP1.IO21, WeMos_D1_Mini_OLED_Shield1.D2
  N5: WeMos_D1_Mini_Dual_Base_Shield1.D3_Left, WeMos_D1_Mini_Dual_Base_Shield1.D3_Right, WeMos_D1_Mini_Protoboard_Shield1.D3, WeMos_D1_Mini_Protoboard_Shield1.X7-Y5, TD-er1.RX, MH-ET_Live_Minikit_for_ESP1.IO17, WeMos_D1_Mini_OLED_Shield1.D3
  N6: WeMos_D1_Mini_Dual_Base_Shield1.D4_Left, WeMos_D1_Mini_Dual_Base_Shield1.D4_Right, WeMos_D1_Mini_Protoboard_Shield1.D4, TD-er1.TX, MH-ET_Live_Minikit_for_ESP1.IO16, WeMos_D1_Mini_OLED_Shield1.D4
  N7: WeMos_D1_Mini_Dual_Base_Shield1.D5_Left, WeMos_D1_Mini_Dual_Base_Shield1.D5_Right, WeMos_D1_Mini_Protoboard_Shield1.D5, MH-ET_Live_Minikit_for_ESP1.IO18, WeMos_D1_Mini_OLED_Shield1.D5
  N8: WeMos_D1_Mini_Dual_Base_Shield1.D6_Left, WeMos_D1_Mini_Dual_Base_Shield1.D6_Right, WeMos_D1_Mini_Protoboard_Shield1.D6, MH-ET_Live_Minikit_for_ESP1.IO19, WeMos_D1_Mini_OLED_Shield1.D6
  N9: WeMos_D1_Mini_Dual_Base_Shield1.D7_Left, WeMos_D1_Mini_Dual_Base_Shield1.D7_Right, WeMos_D1_Mini_Protoboard_Shield1.D7, MH-ET_Live_Minikit_for_ESP1.IO23, WeMos_D1_Mini_OLED_Shield1.D7
  N10: WeMos_D1_Mini_Dual_Base_Shield1.D8_Left, WeMos_D1_Mini_Dual_Base_Shield1.D8_Right, WeMos_D1_Mini_Protoboard_Shield1.D8, MH-ET_Live_Minikit_for_ESP1.IO5, WeMos_D1_Mini_OLED_Shield1.D8
  GND: WeMos_D1_Mini_Dual_Base_Shield1.G_Left, WeMos_D1_Mini_Dual_Base_Shield1.G_Right, WeMos_D1_Mini_Protoboard_Shield1.G, WeMos_D1_Mini_Protoboard_Shield1.X7-Y7, TD-er1.GND, MH-ET_Live_Minikit_for_ESP1.GND, WeMos_D1_Mini_OLED_Shield1.G
  N11: WeMos_D1_Mini_Dual_Base_Shield1.RST_Left, WeMos_D1_Mini_Dual_Base_Shield1.RST_Right, WeMos_D1_Mini_Protoboard_Shield1.RST, WeMos_D1_Mini_Protoboard_Shield1.X2-Y1, WeMos_D1_Mini_Protoboard_Shield1.X3-Y1, D1.anode, MH-ET_Live_Minikit_for_ESP1.RST, WeMos_D1_Mini_OLED_Shield1.RST
  N12: WeMos_D1_Mini_Dual_Base_Shield1.RX_Left, WeMos_D1_Mini_Dual_Base_Shield1.RX_Right, WeMos_D1_Mini_Protoboard_Shield1.RX, MH-ET_Live_Minikit_for_ESP1.RXD, WeMos_D1_Mini_OLED_Shield1.RX
  N13: WeMos_D1_Mini_Dual_Base_Shield1.TX_Left, WeMos_D1_Mini_Dual_Base_Shield1.TX_Right, WeMos_D1_Mini_Protoboard_Shield1.TX, MH-ET_Live_Minikit_for_ESP1.TXD, WeMos_D1_Mini_OLED_Shield1.TX

custom parts:
  MH-ET Live Minikit for ESP32: MH-ET Live Minikit for ESP32 ( http://mh.nodebb.com/topic/8/mh-et-live-minikit-for-esp32/2/) PCB footprint is invalid.
